// Logisim project iter_mult.circ as structural Verilog
module main (
  input  m,
  input  n
);

  wire clock_1_out, data_1_cmp;
  wire [1:0] undriven;

  Clock clock_1 (.out(clock_1_out));
  DATA data_1 (.n(m), .m(n), .clck(clock_1_out), .Q(undriven), .cmp(data_1_cmp));
endmodule

module DATA (
  input  n,
  input  m,
  input  clck,
  input  [1:0] Q,
  output cmp
);

  wire adder_1_out, d_ff_2_q, multiplexer_1_out, not_1_out;

  not not_1 (not_1_out, clck);
  D_Flip_Flop d_ff_1 (.clk(clck), .D(d_ff_2_q), .Q(cmp));  // open: Qn, preset, en, reset
  Adder #(.width(1)) adder_1 (.a(cmp), .b(1'b1), .out(adder_1_out));  // open: cin, cout
  Multiplexer #(.select(2), .enable("false")) multiplexer_1 (
    .in0(1'b0), .in1(m), .in2(adder_1_out), .in3(cmp), .out(multiplexer_1_out), .sel(Q));
  D_Flip_Flop d_ff_2 (.clk(not_1_out), .D(multiplexer_1_out), .Q(d_ff_2_q));  // open: Qn, preset, en, reset
endmodule

module CTRL_INTER (
  input  req,
  input  cmp,
  input  [1:0] Q,
  output [1:0] Q_prime
);

  wire and_1_out, and_2_out, and_3_out, and_4_out, and_5_out;

  and and_1 (and_1_out, req, Q[0]);
  and and_2 (and_2_out, req, Q[1]);
  or or_1 (Q_prime[1], and_1_out, and_2_out);
  and and_3 (and_3_out, req, ~Q[1], ~Q[0]);  // AND_Gate
  and and_4 (and_4_out, req, Q[1], Q[0]);
  and and_5 (and_5_out, req, ~cmp, Q[1]);  // AND_Gate
  or or_2 (Q_prime[0], and_3_out, and_4_out, and_5_out);
endmodule
