// Logisim project traffic_lights.circ as structural Verilog: 1 circuit, main circuit main
module main (
);

  wire adder_1_cout, adder_1_out, adder_2_cout, adder_2_out, adder_3_out, and_1_out, and_2_out, and_3_out,
       and_4_out, and_5_out, and_6_out, and_7_out, clock_1_out, d_ff_1_q, d_ff_2_q, d_ff_2_qn, d_ff_3_q,
       d_ff_4_q, d_ff_4_qn, d_ff_5_q, d_ff_6_q, d_ff_6_qn, not_1_out, not_2_out, not_3_out, not_4_out,
       or_1_out, or_2_out, xor_1_out, xor_2_out;

  Clock clock_1 (.out(clock_1_out));
  not not_1 (not_1_out, clock_1_out);
  D_Flip_Flop d_ff_1 (.clk(not_1_out), .D(adder_1_out), .Q(d_ff_1_q), .reset(and_7_out));  // open: Qn, preset, en
  Adder #(.width(1)) adder_1 (.a(1'b1), .b(d_ff_2_q), .out(adder_1_out), .cin(1'b0), .cout(adder_1_cout));
  D_Flip_Flop d_ff_2 (.clk(clock_1_out), .D(d_ff_1_q), .Q(d_ff_2_q), .Qn(d_ff_2_qn));  // open: preset, en, reset
  D_Flip_Flop d_ff_3 (.clk(not_1_out), .D(adder_2_out), .Q(d_ff_3_q), .reset(and_7_out));  // open: Qn, preset, en
  Adder #(.width(1)) adder_2 (.a(1'b0), .b(d_ff_4_q), .out(adder_2_out), .cin(adder_1_cout), .cout(adder_2_cout));
  D_Flip_Flop d_ff_4 (.clk(clock_1_out), .D(d_ff_3_q), .Q(d_ff_4_q), .Qn(d_ff_4_qn));  // open: preset, en, reset
  D_Flip_Flop d_ff_5 (.clk(not_1_out), .D(adder_3_out), .Q(d_ff_5_q), .reset(and_7_out));  // open: Qn, preset, en
  Adder #(.width(1)) adder_3 (.a(1'b0), .b(d_ff_6_q), .out(adder_3_out), .cin(adder_2_cout));  // open: cout
  D_Flip_Flop d_ff_6 (.clk(clock_1_out), .D(d_ff_5_q), .Q(d_ff_6_q), .Qn(d_ff_6_qn));  // open: preset, en, reset
  or or_1 (or_1_out, d_ff_2_q, d_ff_6_qn);
  xor xor_1 (xor_1_out, d_ff_4_q, d_ff_6_q);
  and and_1 (and_1_out, or_1_out, d_ff_4_qn);
  and and_2 (and_2_out, xor_1_out, d_ff_2_qn);
  and and_3 (and_3_out, d_ff_2_q, d_ff_4_q, d_ff_6_qn);
  or or_2 (or_2_out, d_ff_2_q, d_ff_6_q);
  xor xor_2 (xor_2_out, d_ff_4_q, d_ff_6_q);
  and and_4 (and_4_out, d_ff_4_qn, d_ff_2_q);
  and and_5 (and_5_out, d_ff_2_qn, d_ff_4_qn, d_ff_6_qn);
  not not_2 (not_2_out, and_1_out);
  not not_3 (not_3_out, and_2_out);
  not not_4 (not_4_out, and_3_out);
  and and_6 (and_6_out, or_2_out, xor_2_out);
  and and_7 (and_7_out, not_2_out, not_3_out, not_4_out);
  LED led_1 (.in(and_1_out));
  LED led_2 (.in(and_2_out));
  LED led_3 (.in(and_3_out));
  LED led_4 (.in(and_6_out));
  LED led_5 (.in(and_4_out));
  LED led_6 (.in(and_5_out));
endmodule
