// Logisim project plexors.circ as structural Verilog
module _4_1MUX (
  input  in_1,
  input  in_2,
  input  in_3,
  input  in_4,
  input  in_5,
  input  in_6,
  output out_7
);

  wire n2_1mux_1_out_4, n2_1mux_2_out_4;

  _2_1MUX u_2_1mux_1 (.x(in_1), .y(in_2), .c(in_5), .out_4(n2_1mux_1_out_4));
  _2_1MUX u_2_1mux_2 (.x(in_3), .y(in_4), .c(in_5), .out_4(n2_1mux_2_out_4));
  _2_1MUX u_2_1mux_3 (.x(n2_1mux_1_out_4), .y(n2_1mux_2_out_4), .c(in_6), .out_4(out_7));
endmodule

module _2_1MUX (
  input  x,
  input  y,
  input  c,
  output out_4
);

  wire and_1_out, and_2_out, not_1_out;

  not not_1 (not_1_out, c);
  and and_1 (and_1_out, x, not_1_out);
  and and_2 (and_2_out, y, c);
  or or_1 (out_4, and_1_out, and_2_out);
endmodule
