// Logisim project sr-latch.circ as structural Verilog
module sr1 (
  input  S,
  input  R,
  output nQ,
  output Q
);

  nor nor_1 (nQ, S, Q);
  nor nor_2 (Q, nQ, R);
endmodule

module sr2 (
  input  D,
  input  en,
  output nQ,
  output Q
);

  wire and_1_out, and_2_out, not_1_out;

  not not_1 (not_1_out, D);
  and and_1 (and_1_out, D, en);
  and and_2 (and_2_out, en, not_1_out);
  nor nor_1 (nQ, and_1_out, Q);
  nor nor_2 (Q, nQ, and_2_out);

  // Notes on the sheet:
  //   S'
  //   R'
endmodule

module sr3 (
  input  D,
  input  en,
  output S,
  output nQ,
  output Q,
  output R
);

  wire nand_1_out, nand_2_out, nand_3_out, nand_6_out, nand_7_out, nand_8_out, nand_9_out, nand_12_out,
       nand_13_out;

  nand nand_1 (nand_1_out, D, en);
  nand nand_2 (nand_2_out, D, D);
  nand nand_3 (nand_3_out, nand_2_out, en);
  nand nand_4 (S, nand_1_out, nand_1_out);
  nand nand_5 (R, nand_3_out, nand_3_out);
  nand nand_6 (nand_6_out, S, S);
  nand nand_7 (nand_7_out, R, R);
  nand nand_8 (nand_8_out, nand_6_out, nand_13_out);
  nand nand_9 (nand_9_out, nand_12_out, nand_7_out);
  nand nand_10 (nQ, nand_8_out, nand_8_out);
  nand nand_11 (Q, nand_9_out, nand_9_out);
  nand nand_12 (nand_12_out, nQ, nQ);
  nand nand_13 (nand_13_out, Q, Q);
endmodule

module sr4 (
  input  D,
  input  en,
  output S,
  output nQ,
  output Q,
  output R
);

  wire not_1_out;

  nand nand_1 (S, D, en);
  not not_1 (not_1_out, D);
  nand nand_2 (R, not_1_out, en);
  nand nand_3 (nQ, S, Q);
  nand nand_4 (Q, nQ, R);
endmodule
