// Logisim project adders.circ as structural Verilog: 5 circuits, main circuit 2-1ADD
// 2ADD
module _2_1ADD (
  input  x0,
  input  y0,
  input  ci,
  output s,
  output c_o
);

  wire and_1_out, and_2_out, xor_1_out;

  xor xor_1 (xor_1_out, x0, y0);
  xor xor_2 (s, xor_1_out, ci);
  and and_1 (and_1_out, xor_1_out, ci);
  or or_1 (c_o, and_1_out, and_2_out);
  and and_2 (and_2_out, y0, x0);
endmodule

module _4_1ADD (
  input  x0,
  input  y0,
  input  x1,
  input  y1,
  input  x2,
  input  y2,
  input  x3,
  input  y3,
  output r0,
  output r_1,
  output r_2,
  output r_3,
  output overflow
);

  wire n2_1add_1_c_o, n2_1add_2_c_o, n2_1add_3_c_o;

  _2_1ADD u_2_1add_1 (.x0(x0), .y0(y0), .ci(1'b0), .s(r0), .c_o(n2_1add_1_c_o));
  _2_1ADD u_2_1add_2 (.x0(x1), .y0(y1), .ci(n2_1add_1_c_o), .s(r_1), .c_o(n2_1add_2_c_o));
  _2_1ADD u_2_1add_3 (.x0(x2), .y0(y2), .ci(n2_1add_2_c_o), .s(r_2), .c_o(n2_1add_3_c_o));
  _2_1ADD u_2_1add_4 (.x0(x3), .y0(y3), .ci(n2_1add_3_c_o), .s(r_3), .c_o(overflow));
  LED _1 (.in(r0));
  LED _2 (.in(r_1));
  LED _4 (.in(r_2));
  LED _8 (.in(r_3));
  LED _16 (.in(overflow));
endmodule

// DLATCH
module D_LATCH_NAND (
  input  D,
  input  en,
  output Q,
  output nQ
);

  wire nand_1_out, nand_2_out;

  nand nand_1 (nand_1_out, D, en);
  nand nand_2 (nand_2_out, nand_1_out, en);
  nand nand_3 (Q, nand_1_out, nQ);
  nand nand_4 (nQ, Q, nand_2_out);
endmodule

// 4REG
module _2_COUNT (
  input  reset
);

  wire clock_1_out, d_latch_nand_1_q, d_latch_nand_2_q, d_latch_nand_3_q, d_latch_nand_4_q, n2_1add_1_c_o,
       n2_1add_1_s, n2_1add_2_c_o, n2_1add_2_s, not_1_out;

  Clock clock_1 (.out(clock_1_out));
  not not_1 (not_1_out, clock_1_out);
  // NOT_Gate not_2 has open pins: in=reset, out=open
  D_LATCH_NAND d_latch_nand_1 (.D(n2_1add_1_s), .en(not_1_out), .Q(d_latch_nand_1_q));  // open: nQ
  _2_1ADD u_2_1add_1 (.x0(d_latch_nand_2_q), .y0(1'b1), .ci(1'b0), .s(n2_1add_1_s), .c_o(n2_1add_1_c_o));
  D_LATCH_NAND d_latch_nand_2 (.D(d_latch_nand_1_q), .en(clock_1_out), .Q(d_latch_nand_2_q));  // open: nQ
  D_LATCH_NAND d_latch_nand_3 (.D(n2_1add_2_s), .en(not_1_out), .Q(d_latch_nand_3_q));  // open: nQ
  _2_1ADD u_2_1add_2 (.x0(d_latch_nand_4_q), .y0(1'b0), .ci(n2_1add_1_c_o), .s(n2_1add_2_s), .c_o(n2_1add_2_c_o));
  D_LATCH_NAND d_latch_nand_4 (.D(d_latch_nand_3_q), .en(clock_1_out), .Q(d_latch_nand_4_q));  // open: nQ
endmodule

module D_LATCH_RESET (
  input  D,
  input  en,
  output Q,
  output nQ
);

  wire nand_1_out, nand_2_out;

  nand nand_1 (nand_1_out, D, en);
  nand nand_2 (nand_2_out, nand_1_out, en);
  nand nand_3 (Q, nand_1_out, nQ);
  nand nand_4 (nQ, Q, nand_2_out);
endmodule
