// Logisim project broken.circ as structural Verilog: 21 circuits, main circuit NOT
module main (
  input  in_1,
  output [3:0] out_2
);

  wire clock_1_out;
  wire [3:0] undriven;
  wire [7:0] disp_4_1_out_2;

  Clock clock_1 (.out(clock_1_out));
  CNT_4B cnt_4b_1 (.clck(clock_1_out), .reset(in_1), .mod(4'b1010), .cnt(out_2));
  DISP_4 disp_4_1 (.in_1(out_2), .out_2(disp_4_1_out_2));
  _7_Segment_Display u_7_segment_display_1 (
    .g(disp_4_1_out_2[3]), .f(disp_4_1_out_2[2]), .a(disp_4_1_out_2[1]), .b(disp_4_1_out_2[0]),
    .e(undriven[3]), .d(undriven[2]), .c(undriven[1]), .dp(undriven[0]));
endmodule

module NOT (
  input  x,
  input  in_2,
  output nx
);

  wire transistor_2_out;

  Transistor transistor_1 (.in(1'b1), .out(nx), .gate(x));
  Transistor #(.\type ("n")) transistor_2 (.in(nx), .out(transistor_2_out), .gate(x));
  Pull_Resistor pull_resistor_1 (.node(nx));
  // also tied to GND on the sheet: transistor_2_out

  // Notes on the sheet:
  //   x: pull=down
  //   nx: pull=up
endmodule

module NAND (
  input  x,
  input  y,
  output n_x_y
);

  wire transistor_3_out, transistor_4_out;

  Transistor transistor_1 (.in(1'b1), .out(n_x_y), .gate(x));
  Transistor transistor_2 (.in(1'b1), .out(n_x_y), .gate(y));
  Pull_Resistor pull_resistor_1 (.node(n_x_y));
  Transistor #(.\type ("n")) transistor_3 (.in(n_x_y), .out(transistor_3_out), .gate(x));
  Transistor #(.\type ("n")) transistor_4 (.in(transistor_3_out), .out(transistor_4_out), .gate(y));
  // also tied to GND on the sheet: transistor_4_out

  // Notes on the sheet:
  //   y: pull=down
  //   x: pull=down
endmodule

module NOR (
  input  x,
  input  y,
  output n_x_y
);

  wire transistor_1_out, transistor_2_out;

  Transistor #(.\type ("n")) transistor_1 (.in(n_x_y), .out(transistor_1_out), .gate(x));
  Transistor transistor_2 (.in(1'b1), .out(transistor_2_out), .gate(x));
  Transistor transistor_3 (.in(transistor_2_out), .out(n_x_y), .gate(y));
  Pull_Resistor pull_resistor_1 (.node(n_x_y));
  Transistor #(.\type ("n")) transistor_4 (.in(n_x_y), .out(transistor_1_out), .gate(y));
  // also tied to GND on the sheet: transistor_1_out

  // Notes on the sheet:
  //   n_x_y: pull=up
  //   x: pull=down
  //   y: pull=down
endmodule

module AND (
  input  x,
  input  y,
  output x_y
);

  wire nand_1_n_x_y;

  NAND nand_1 (.x(x), .y(y), .n_x_y(nand_1_n_x_y));
  NOT not_1 (.x(nand_1_n_x_y), .nx(x_y));  // open: in_2

  // Notes on the sheet:
  //   y: pull=down
  //   x_y: pull=up
  //   x: pull=down
endmodule

module OR (
  input  x,
  input  y,
  output x_y
);

  wire nor_1_n_x_y;

  NOR nor_1 (.x(x), .y(y), .n_x_y(nor_1_n_x_y));
  NOT not_1 (.x(nor_1_n_x_y), .nx(x_y));  // open: in_2
endmodule

module XOR (
  input  x,
  input  y,
  output out_3
);

  wire nand_1_n_x_y, or_1_x_y;

  OR or_1 (.x(x), .y(y), .x_y(or_1_x_y));
  NAND nand_1 (.x(x), .y(y), .n_x_y(nand_1_n_x_y));
  AND and_1 (.x(or_1_x_y), .y(nand_1_n_x_y), .x_y(out_3));

  // Notes on the sheet:
  //   x: pull=down
  //   y: pull=down
endmodule

// MUX
module _2MUX_1B (
  input  x,
  input  y,
  input  c,
  output out_4
);

  wire and_1_x_y, and_2_x_y, not_1_nx;

  NOT not_1 (.x(c), .nx(not_1_nx));  // open: in_2
  OR or_1 (.x(and_1_x_y), .y(and_2_x_y), .x_y(out_4));
  AND and_1 (.x(x), .y(not_1_nx), .x_y(and_1_x_y));
  AND and_2 (.x(y), .y(c), .x_y(and_2_x_y));

  // Notes on the sheet:
  //   x: pull=down
  //   c: pull=down
  //   y: pull=down
endmodule

// MUX
module _2MUX_4B (
  input  [3:0] x,
  input  [3:0] y,
  input  c,
  output [3:0] out_4
);

  _2MUX_1B u_2mux_1b_1 (.x(x[0]), .y(y[0]), .c(c), .out_4(out_4[0]));
  _2MUX_1B u_2mux_1b_2 (.x(x[1]), .y(y[1]), .c(c), .out_4(out_4[1]));
  _2MUX_1B u_2mux_1b_3 (.x(x[2]), .y(y[2]), .c(c), .out_4(out_4[2]));
  _2MUX_1B u_2mux_1b_4 (.x(x[3]), .y(y[3]), .c(c), .out_4(out_4[3]));
endmodule

// 2+1B
module _2ADD_1B (
  input  c_in,
  input  x,
  input  y,
  output s,
  output c_out
);

  wire and_1_x_y, and_2_x_y, xor_1_out_3;

  XOR xor_1 (.x(x), .y(y), .out_3(xor_1_out_3));
  XOR xor_2 (.x(xor_1_out_3), .y(c_in), .out_3(s));
  AND and_1 (.x(x), .y(y), .x_y(and_1_x_y));
  OR or_1 (.x(and_1_x_y), .y(and_2_x_y), .x_y(c_out));
  AND and_2 (.x(xor_1_out_3), .y(c_in), .x_y(and_2_x_y));

  // Notes on the sheet:
  //   y: pull=down
  //   x: pull=down
  //   c_in: pull=down
endmodule

// 2+4B
module _2ADD_4B (
  input  c_in,
  input  [3:0] x,
  input  [3:0] y,
  output c_out,
  output [3:0] out_5
);

  wire n2add_1b_1_c_out, n2add_1b_2_c_out, n2add_1b_3_c_out;

  _2ADD_1B u_2add_1b_1 (.x(x[0]), .y(y[0]), .c_in(c_in), .c_out(n2add_1b_1_c_out), .s(out_5[0]));
  _2ADD_1B u_2add_1b_2 (.x(x[1]), .y(y[1]), .c_in(n2add_1b_1_c_out), .c_out(n2add_1b_2_c_out), .s(out_5[1]));
  _2ADD_1B u_2add_1b_3 (.x(x[2]), .y(y[2]), .c_in(n2add_1b_2_c_out), .c_out(n2add_1b_3_c_out), .s(out_5[2]));
  _2ADD_1B u_2add_1b_4 (.x(x[3]), .y(y[3]), .c_in(n2add_1b_3_c_out), .c_out(c_out), .s(out_5[3]));

  // Notes on the sheet:
  //   x: pull=down
  //   y: pull=down
  //   c_in: pull=down
endmodule

// 2-1B
module _2SUB_1B (
  input  x,
  input  y,
  input  b_out,
  output s,
  output b_in
);

  wire and_1_x_y, and_2_x_y, not_1_nx, or_1_x_y, xor_1_out_3;

  XOR xor_1 (.x(x), .y(y), .out_3(xor_1_out_3));
  NOT not_1 (.x(x), .nx(not_1_nx));  // open: in_2
  OR or_1 (.x(not_1_nx), .y(y), .x_y(or_1_x_y));
  AND and_1 (.x(not_1_nx), .y(y), .x_y(and_1_x_y));
  XOR xor_2 (.x(xor_1_out_3), .y(b_out), .out_3(s));
  AND and_2 (.x(or_1_x_y), .y(b_out), .x_y(and_2_x_y));
  OR or_2 (.x(and_2_x_y), .y(and_1_x_y), .x_y(b_in));

  // Notes on the sheet:
  //   x: pull=down
  //   b_out: pull=down
  //   y: pull=down
endmodule

// 2-4B
module _2SUB_4B (
  input  b_out,
  input  [3:0] x,
  input  [3:0] y,
  output b_in,
  output [3:0] out_5
);

  wire n2sub_1b_1_b_in, n2sub_1b_2_b_in, n2sub_1b_3_b_in;

  _2SUB_1B u_2sub_1b_1 (.x(x[0]), .y(y[0]), .b_out(b_out), .b_in(n2sub_1b_1_b_in), .s(out_5[0]));
  _2SUB_1B u_2sub_1b_2 (.x(x[1]), .y(y[1]), .b_out(n2sub_1b_1_b_in), .b_in(n2sub_1b_2_b_in), .s(out_5[1]));
  _2SUB_1B u_2sub_1b_3 (.x(x[2]), .y(y[2]), .b_out(n2sub_1b_2_b_in), .b_in(n2sub_1b_3_b_in), .s(out_5[2]));
  _2SUB_1B u_2sub_1b_4 (.x(x[3]), .y(y[3]), .b_out(n2sub_1b_3_b_in), .b_in(b_in), .s(out_5[3]));

  // Notes on the sheet:
  //   b_out: pull=down
  //   y: pull=down
  //   x: pull=down
endmodule

// 2<1B
module _2LST_1B (
  input  x,
  input  y,
  output x___y
);

  wire not_1_nx;

  NOT not_1 (.x(x), .nx(not_1_nx));  // open: in_2
  AND and_1 (.x(not_1_nx), .y(y), .x_y(x___y));

  // Notes on the sheet:
  //   x: pull=down
  //   y: pull=down
endmodule

// 2=1B
module _2EQT_1B (
  input  x,
  input  y,
  output x___y
);

  wire xor_1_out_3;

  XOR xor_1 (.x(x), .y(y), .out_3(xor_1_out_3));
  NOT not_1 (.x(xor_1_out_3), .nx(x___y));  // open: in_2

  // Notes on the sheet:
  //   y: pull=down
  //   x: pull=down
endmodule

// 2=4B
module _2EQT_4B (
  input  [3:0] x,
  input  [3:0] y,
  output x___y
);

  wire and_1_x_y, and_2_x_y, n2eqt_1b_1_x___y, n2eqt_1b_2_x___y, n2eqt_1b_3_x___y, n2eqt_1b_4_x___y;

  _2EQT_1B u_2eqt_1b_1 (.x(x[0]), .y(y[0]), .x___y(n2eqt_1b_1_x___y));
  _2EQT_1B u_2eqt_1b_2 (.x(x[1]), .y(y[1]), .x___y(n2eqt_1b_2_x___y));
  _2EQT_1B u_2eqt_1b_3 (.x(x[2]), .y(y[2]), .x___y(n2eqt_1b_3_x___y));
  _2EQT_1B u_2eqt_1b_4 (.x(x[3]), .y(y[3]), .x___y(n2eqt_1b_4_x___y));
  AND and_1 (.x(n2eqt_1b_1_x___y), .y(n2eqt_1b_2_x___y), .x_y(and_1_x_y));
  AND and_2 (.x(n2eqt_1b_3_x___y), .y(n2eqt_1b_4_x___y), .x_y(and_2_x_y));
  AND and_3 (.x(and_1_x_y), .y(and_2_x_y), .x_y(x___y));
endmodule

// >>1
module LSHFT1B (
  input  [1:0] in_1,
  output [1:0] out_2
);


  assign out_2 = {1'b0, in_1[1]};

  // Notes on the sheet:
  //   in_1: pull=down
endmodule

// DL1
module DLTCH_1B (
  input  D,
  input  en,
  output Q,
  output nQ
);

  wire nand_1_out, nand_2_out, not_1_out;

  not not_1 (not_1_out, D);
  nand nand_1 (nand_1_out, D, en);
  nand nand_2 (nand_2_out, not_1_out, en);
  nand nand_3 (Q, nand_1_out, nQ);
  nand nand_4 (nQ, Q, nand_2_out);

  // Notes on the sheet:
  //   en: pull=down
  //   nQ: pull=up
  //   Q: pull=up
  //   D: pull=down
endmodule

// DL4
module DLTCH_4B (
  input  [3:0] in_1,
  input  en,
  output [3:0] out_3,
  output [3:0] out_4
);

  DLTCH_1B dltch_1b_1 (.D(in_1[0]), .en(en), .Q(out_3[0]), .nQ(out_4[0]));
  DLTCH_1B dltch_1b_2 (.D(in_1[1]), .en(en), .Q(out_3[1]), .nQ(out_4[1]));
  DLTCH_1B dltch_1b_3 (.D(in_1[2]), .en(en), .Q(out_3[2]), .nQ(out_4[2]));
  DLTCH_1B dltch_1b_4 (.D(in_1[3]), .en(en), .Q(out_3[3]), .nQ(out_4[3]));
endmodule

// CNT4
module CNT_4B (
  input  clck,
  input  reset,
  input  [3:0] mod,
  output [3:0] cnt
);

  wire n2eqt_4b_1_x___y, not_1_nx, or_1_x_y;
  wire [3:0] dltch_4b_2_out_3, n2add_4b_1_out_5, n2mux_4b_1_out_4, n2sub_4b_1_out_5;

  NOT not_1 (.x(clck), .nx(not_1_nx));  // open: in_2
  _2EQT_4B u_2eqt_4b_1 (.x(n2sub_4b_1_out_5), .y(cnt), .x___y(n2eqt_4b_1_x___y));
  _2SUB_4B u_2sub_4b_1 (.x(mod), .y(4'b0001), .out_5(n2sub_4b_1_out_5));  // open: b_out, b_in
  DLTCH_4B dltch_4b_1 (.in_1(dltch_4b_2_out_3), .en(clck), .out_3(cnt));  // open: out_4
  _2ADD_4B u_2add_4b_1 (.x(cnt), .y(4'b0001), .c_in(1'b0), .out_5(n2add_4b_1_out_5));  // open: c_out
  OR or_1 (.x(reset), .y(n2eqt_4b_1_x___y), .x_y(or_1_x_y));
  _2MUX_4B u_2mux_4b_1 (.x(n2add_4b_1_out_5), .y(4'b0000), .c(or_1_x_y), .out_4(n2mux_4b_1_out_4));
  DLTCH_4B dltch_4b_2 (.in_1(n2mux_4b_1_out_4), .en(not_1_nx), .out_3(dltch_4b_2_out_3));  // open: out_4

  // Notes on the sheet:
  //   mod: pull=down
  //   reset: pull=down
  //   clck: pull=down
endmodule

module DISP_4 (
  input  [3:0] in_1,
  output [7:0] out_2
);

  wire and_1_x_y, and_2_x_y, and_3_x_y, and_4_x_y, and_5_x_y, and_6_x_y, and_7_x_y, and_8_x_y, nand_1_n_x_y,
       nand_2_n_x_y, nand_3_n_x_y, nor_1_n_x_y, nor_2_n_x_y, nor_3_n_x_y, nor_4_n_x_y, nor_5_n_x_y,
       nor_6_n_x_y, not_1_nx, not_2_nx, not_3_nx, xor_1_out_3, xor_2_out_3;

  XOR xor_1 (.x(nand_1_n_x_y), .y(nand_2_n_x_y), .out_3(xor_1_out_3));
  NAND nand_1 (.x(in_1[0]), .y(in_1[2]), .n_x_y(nand_1_n_x_y));
  NAND nand_2 (.x(in_1[2]), .y(in_1[1]), .n_x_y(nand_2_n_x_y));
  NOT not_1 (.x(in_1[3]), .nx(not_1_nx));  // open: in_2
  AND and_1 (.x(nor_1_n_x_y), .y(in_1[0]), .x_y(and_1_x_y));
  NOR nor_1 (.x(in_1[1]), .y(in_1[2]), .n_x_y(nor_1_n_x_y));
  NOR nor_2 (.x(in_1[0]), .y(in_1[1]), .n_x_y(nor_2_n_x_y));
  AND and_2 (.x(nor_2_n_x_y), .y(in_1[2]), .x_y(and_2_x_y));
  NAND nand_3 (.x(in_1[0]), .y(in_1[1]), .n_x_y(nand_3_n_x_y));
  AND and_3 (.x(nand_3_n_x_y), .y(in_1[2]), .x_y(and_3_x_y));
  NOR nor_3 (.x(in_1[0]), .y(in_1[1]), .n_x_y(nor_3_n_x_y));
  AND and_4 (.x(nor_3_n_x_y), .y(nor_4_n_x_y), .x_y(and_4_x_y));
  NOR nor_4 (.x(in_1[2]), .y(in_1[3]), .n_x_y(nor_4_n_x_y));
  AND and_5 (.x(in_1[0]), .y(in_1[1]), .x_y(and_5_x_y));
  AND and_6 (.x(not_2_nx), .y(in_1[2]), .x_y(and_6_x_y));
  NOT not_2 (.x(in_1[3]), .nx(not_2_nx));  // open: in_2
  NOR nor_5 (.x(in_1[3]), .y(in_1[2]), .n_x_y(nor_5_n_x_y));
  NOR nor_6 (.x(in_1[1]), .y(not_3_nx), .n_x_y(nor_6_n_x_y));
  NOT not_3 (.x(in_1[0]), .nx(not_3_nx));  // open: in_2
  NOT not_4 (.x(xor_1_out_3), .nx(out_2[0]));  // open: in_2
  NAND nand_4 (.x(not_1_nx), .y(xor_2_out_3), .n_x_y(out_2[1]));
  XOR xor_2 (.x(and_1_x_y), .y(and_2_x_y), .out_3(xor_2_out_3));
  OR or_1 (.x(and_3_x_y), .y(in_1[3]), .x_y(out_2[2]));
  OR or_2 (.x(and_4_x_y), .y(and_7_x_y));  // open: x_y
  AND and_7 (.x(and_5_x_y), .y(and_6_x_y), .x_y(and_7_x_y));
  AND and_8 (.x(nor_5_n_x_y), .y(nor_6_n_x_y), .x_y(and_8_x_y));
endmodule
