// Logisim project countermachine.circ as structural Verilog
// 4
module main (
  input  [3:0] in_1,
  input  [3:0] in_2,
  input  [3:0] in_3,
  input  [3:0] in_4,
  output [3:0] out_5,
  output [3:0] out_6,
  output [3:0] out_7,
  output [3:0] out_8
);

  wire clock_1_out;
  wire [1:0] arithmetic_1_out_7;
  wire [3:0] multiplexer_1_out;

  Clock clock_1 (.out(clock_1_out));
  Multiplexer #(.select(2), .width(4)) multiplexer_1 (
    .in0(in_1), .in1(in_2), .in2(in_3), .in3(in_4), .out(multiplexer_1_out), .sel(arithmetic_1_out_7));  // open: en
  DotMatrix #(.matrixcols(4), .matrixrows(4)) dotmatrix_1 (.col0(out_5), .col1(out_6), .col2(out_7), .col3(out_8));
  arithmetic arithmetic_1 (
    .\input (multiplexer_1_out), .clock(clock_1_out), .out_7(arithmetic_1_out_7), .r0(out_5), .r1(out_6),
    .r2(out_7), .r3(out_8));
endmodule

module arithmetic (
  input  [3:0] \input ,
  input  clock,
  output [3:0] r0,
  output [3:0] r1,
  output [3:0] r2,
  output [3:0] r3,
  output [1:0] out_7
);

  wire and_1_out, demultiplexer_2_out0, demultiplexer_2_out1, demultiplexer_2_out2, demultiplexer_2_out3,
       demultiplexer_5_out0, demultiplexer_5_out1, demultiplexer_5_out2, demultiplexer_5_out3, I____JZ,
       not_1_out, r0____0;
  wire [1:0] adder_1_out, multiplexer_1_out, register_2_q;
  wire [3:0] adder_2_out, demultiplexer_1_out0, demultiplexer_1_out1, demultiplexer_1_out2,
       demultiplexer_1_out3, demultiplexer_3_out0, demultiplexer_3_out1, demultiplexer_4_out0,
       demultiplexer_4_out1, demultiplexer_4_out2, demultiplexer_4_out3, multiplexer_2_out,
       multiplexer_3_out, multiplexer_4_out, register_3_q, register_4_q, register_5_q, register_6_q,
       subtractor_1_out;

  and and_1 (and_1_out, ~r0____0, I____JZ);  // AND_Gate
  not not_1 (not_1_out, clock);
  Register #(.width(2)) register_1 (.D(multiplexer_1_out), .Q(out_7), .clk(clock));  // open: en, clr
  Adder #(.width(2)) adder_1 (.a(2'b01), .b(register_2_q), .out(adder_1_out));  // open: cin, cout
  Register #(.width(2)) register_2 (.D(out_7), .Q(register_2_q), .clk(not_1_out));  // open: en, clr
  Multiplexer #(.width(2)) multiplexer_1 (
    .in0(adder_1_out), .in1(\input [1:0]), .out(multiplexer_1_out), .sel(and_1_out));  // open: en
  Demultiplexer #(.select(2), .width(4)) demultiplexer_1 (
    .out0(demultiplexer_1_out0), .out1(demultiplexer_1_out1), .out2(demultiplexer_1_out2),
    .out3(demultiplexer_1_out3), .in(multiplexer_4_out), .sel(\input [1:0]));  // open: en
  Demultiplexer #(.select(2)) demultiplexer_2 (
    .out0(demultiplexer_2_out0), .out1(demultiplexer_2_out1), .out2(demultiplexer_2_out2),
    .out3(demultiplexer_2_out3), .in(clock), .sel(\input [1:0]));  // open: en
  Register #(.width(4), .trigger("falling")) register_3 (
    .D(demultiplexer_1_out0), .Q(register_3_q), .clk(demultiplexer_2_out0));  // open: en, clr
  Register #(.width(4), .trigger("falling")) register_4 (
    .D(demultiplexer_1_out1), .Q(register_4_q), .clk(demultiplexer_2_out1));  // open: en, clr
  Register #(.width(4), .trigger("falling")) register_5 (
    .D(demultiplexer_1_out2), .Q(register_5_q), .clk(demultiplexer_2_out2));  // open: en, clr
  Register #(.width(4), .trigger("falling")) register_6 (
    .D(demultiplexer_1_out3), .Q(register_6_q), .clk(demultiplexer_2_out3));  // open: en, clr
  Multiplexer #(.select(2), .width(4)) multiplexer_2 (
    .in0(register_3_q), .in1(register_4_q), .in2(register_5_q), .in3(register_6_q), .out(multiplexer_2_out),
    .sel(\input [1:0]));  // open: en
  Demultiplexer #(.select(2), .width(4)) demultiplexer_3 (
    .out0(demultiplexer_3_out0), .out1(demultiplexer_3_out1), .in(multiplexer_2_out), .sel(\input [3:2]));  // open: out2, out3, en
  Adder #(.width(4)) adder_2 (.a(demultiplexer_3_out0), .b(4'b0001), .out(adder_2_out));  // open: cin, cout
  Subtractor #(.width(4)) subtractor_1 (
    .a(demultiplexer_3_out1), .b(4'b0001), .out(subtractor_1_out));  // open: bin, bout
  Demultiplexer #(.select(2), .width(4)) demultiplexer_4 (
    .out0(demultiplexer_4_out0), .out1(demultiplexer_4_out1), .out2(demultiplexer_4_out2),
    .out3(demultiplexer_4_out3), .in(multiplexer_3_out), .sel(\input [1:0]));  // open: en
  Multiplexer #(.select(2), .width(4)) multiplexer_3 (
    .in0(adder_2_out), .in1(subtractor_1_out), .out(multiplexer_3_out), .sel(\input [3:2]));  // open: in2, in3, en
  Demultiplexer #(.select(2)) demultiplexer_5 (
    .out0(demultiplexer_5_out0), .out1(demultiplexer_5_out1), .out2(demultiplexer_5_out2),
    .out3(demultiplexer_5_out3), .in(not_1_out), .sel(\input [1:0]));  // open: en
  Register #(.width(4), .trigger("falling")) register_7 (
    .D(demultiplexer_4_out0), .Q(r0), .clk(demultiplexer_5_out0));  // open: en, clr
  Register #(.width(4), .trigger("falling")) register_8 (
    .D(demultiplexer_4_out1), .Q(r1), .clk(demultiplexer_5_out1));  // open: en, clr
  Register #(.width(4), .trigger("falling")) register_9 (
    .D(demultiplexer_4_out2), .Q(r2), .clk(demultiplexer_5_out2));  // open: en, clr
  Register #(.width(4), .trigger("falling")) register_10 (
    .D(demultiplexer_4_out3), .Q(r3), .clk(demultiplexer_5_out3));  // open: en, clr
  Multiplexer #(.select(2), .width(4)) multiplexer_4 (
    .in0(r0), .in1(r1), .in2(r2), .in3(r3), .out(multiplexer_4_out), .sel(\input [1:0]));  // open: en
  Comparator #(.width(4), .mode("unsigned")) comparator_1 (.a(4'b0000), .b(r0), .eq(r0____0));  // open: gt, lt
  Comparator #(.width(2), .mode("unsigned")) comparator_2 (.a(\input [3:2]), .b(2'b10), .eq(I____JZ));  // open: gt, lt

  // Other names for the same wires on the sheet: PC[1:0] = out_7
endmodule

module arithmetic2 (
);

  wire clock_1_out;
  wire [3:0] counter_1_q, undriven, undriven_2;

  Clock clock_1 (.out(clock_1_out));
  Counter #(.width(4), .max('hf)) counter_1 (.Q(counter_1_q), .clk(clock_1_out));  // open: load, D, count, carry, clr
  RAM #(.addrWidth(4), .dataWidth(4)) ram_1 (.addr(undriven));  // open: data, sel, clk, ld, clr
  RAM #(.addrWidth(4), .dataWidth(4)) ram_2 (.addr(undriven_2));  // open: data, sel, clk, ld, clr
endmodule
