// Logisim project countermachine2.circ as structural Verilog: 4 circuits, main circuit main
// 4
module main (
  input  [3:0] in_1,
  input  [3:0] in_2,
  input  [3:0] in_3,
  input  [3:0] in_4,
  output [3:0] out_5,
  output [3:0] out_6,
  output [3:0] out_7,
  output [3:0] out_8
);

  wire clock_1_out;
  wire [1:0] arithmetic_1_out_7;
  wire [3:0] multiplexer_1_out;

  Clock clock_1 (.out(clock_1_out));
  Multiplexer #(.select(2), .width(4)) multiplexer_1 (
    .in0(in_1), .in1(in_2), .in2(in_3), .in3(in_4), .out(multiplexer_1_out), .sel(arithmetic_1_out_7));  // open: en
  DotMatrix #(.matrixcols(4), .matrixrows(4)) dotmatrix_1 (.col0(out_5), .col1(out_6), .col2(out_7), .col3(out_8));
  arithmetic arithmetic_1 (
    .\input (multiplexer_1_out), .clock(clock_1_out), .out_7(arithmetic_1_out_7), .r0(out_5), .r1(out_6),
    .r2(out_7), .r3(out_8));
endmodule

module arithmetic (
  input  [3:0] \input ,
  input  clock,
  output [3:0] r0,
  output [3:0] r1,
  output [3:0] r2,
  output [3:0] r3,
  output [1:0] out_7
);

  wire and_1_out, I____JZ, not_1_out, r0____0;
  wire [1:0] counter_1_q;
  wire [3:0] operator_1_out_3, switch_1_out_4, switch_2_out_4;

  and and_1 (and_1_out, ~r0____0, I____JZ);  // AND_Gate
  // Probe on \input [1:0]
  // Probe on \input [3:2]
  Counter #(.width(2), .max('h3)) counter_1 (
    .load(and_1_out), .D(out_7), .Q(counter_1_q), .clk(clock));  // open: count, carry, clr
  not not_1 (not_1_out, clock);
  Multiplexer #(.width(2)) multiplexer_1 (
    .in0(counter_1_q), .in1(\input [1:0]), .out(out_7), .sel(and_1_out));  // open: en
  switch switch_1 (
    .in_1(switch_2_out_4), .in_2(clock), .out_4(switch_1_out_4), .in_3(\input [1:0]));  // open: out_5, out_6, out_7, out_8
  operator operator_1 (.in_1(switch_1_out_4), .in_2(\input [3:2]), .out_3(operator_1_out_3));
  switch switch_2 (
    .in_1(operator_1_out_3), .in_2(not_1_out), .out_4(switch_2_out_4), .out_5(r0), .out_6(r1), .out_7(r2),
    .out_8(r3), .in_3(\input [1:0]));
  Comparator #(.width(2), .mode("unsigned")) comparator_1 (.a(\input [3:2]), .b(2'b10), .eq(I____JZ));  // open: gt, lt
  Comparator #(.width(4), .mode("unsigned")) comparator_2 (.a(4'b0000), .b(r0), .eq(r0____0));  // open: gt, lt

  // Other names for the same wires on the sheet: PC[1:0] = out_7
endmodule

// OP
module operator (
  input  [3:0] in_1,
  input  [1:0] in_2,
  output [3:0] out_3
);

  wire [3:0] adder_1_out, demultiplexer_1_out0, demultiplexer_1_out1, subtractor_1_out;

  Demultiplexer #(.select(2), .width(4)) demultiplexer_1 (
    .out0(demultiplexer_1_out0), .out1(demultiplexer_1_out1), .in(in_1), .sel(in_2));  // open: out2, out3, en
  Adder #(.width(4)) adder_1 (.a(demultiplexer_1_out0), .b(4'b0001), .out(adder_1_out));  // open: cin, cout
  Subtractor #(.width(4)) subtractor_1 (
    .a(demultiplexer_1_out1), .b(4'b0001), .out(subtractor_1_out));  // open: bin, bout
  Multiplexer #(.select(2), .width(4)) multiplexer_1 (
    .in0(adder_1_out), .in1(subtractor_1_out), .out(out_3), .sel(in_2));  // open: in2, in3, en
endmodule

// SWTCH
module switch (
  input  [3:0] in_1,
  input  in_2,
  input  [1:0] in_3,
  output [3:0] out_4,
  output [3:0] out_5,
  output [3:0] out_6,
  output [3:0] out_7,
  output [3:0] out_8
);

  wire demultiplexer_2_out0, demultiplexer_2_out1, demultiplexer_2_out2, demultiplexer_2_out3, register_6_p1,
       register_6_p2, register_6_p3, undriven;
  wire [3:0] demultiplexer_1_out0, demultiplexer_1_out1, demultiplexer_1_out2, demultiplexer_1_out3;

  Demultiplexer #(.select(2), .width(4)) demultiplexer_1 (
    .out0(demultiplexer_1_out0), .out1(demultiplexer_1_out1), .out2(demultiplexer_1_out2),
    .out3(demultiplexer_1_out3), .in(in_1), .sel(in_3));  // open: en
  Demultiplexer #(.select(2)) demultiplexer_2 (
    .out0(demultiplexer_2_out0), .out1(demultiplexer_2_out1), .out2(demultiplexer_2_out2),
    .out3(demultiplexer_2_out3), .in(in_2), .sel(in_3));  // open: en
  Register #(.width(4), .trigger("falling")) register_1 (
    .D(demultiplexer_1_out0), .Q(out_5), .clk(demultiplexer_2_out0));  // open: en, clr
  Register #(.width(4), .trigger("falling")) register_2 (
    .D(demultiplexer_1_out1), .Q(out_6), .clk(demultiplexer_2_out1));  // open: en, clr
  Register #(.width(4), .trigger("falling")) register_3 (
    .D(demultiplexer_1_out2), .Q(out_7), .clk(demultiplexer_2_out2));  // open: en, clr
  Register #(.width(4), .trigger("falling")) register_4 (
    .D(demultiplexer_1_out3), .Q(out_8), .clk(demultiplexer_2_out3));  // open: en, clr
  Register #(.width(4), .trigger("falling")) register_5 (.clk(register_6_p1));  // open: D, en, Q, clr
  // Register #(.width(4), .trigger("falling")) register_6: pin names not known; wires that end beside it: register_6_p1, register_6_p2, register_6_p3
  Register #(.width(4), .trigger("falling")) register_7 (.clk(register_6_p2));  // open: D, en, Q, clr
  Register #(.width(4), .trigger("falling")) register_8 (.clk(undriven));  // open: D, en, Q, clr
  Multiplexer #(.select(2), .width(4)) multiplexer_1 (
    .in0(out_5), .in1(out_6), .in2(out_7), .in3(out_8), .out(out_4), .sel(in_3));  // open: en
endmodule
