// Logisim project simplecomputer.circ as structural Verilog: 2 circuits, main circuit main
module main (
);

  wire clock_1_out;

  Clock clock_1 (.out(clock_1_out));
  TIMING timing_1 (.CLOCK(clock_1_out));  // open: out_2, out_3, out_4
endmodule

module TIMING (
  input  CLOCK,
  output out_2,
  output out_3,
  output out_4
);

  wire counter_1_carry;
  wire [1:0] counter_1_q;

  Counter #(.width(2), .max('h3)) counter_1 (
    .Q(counter_1_q), .carry(counter_1_carry), .clk(CLOCK), .clr(counter_1_carry));  // open: load, D, count
  Demultiplexer #(.select(2)) demultiplexer_1 (
    .out0(out_2), .out1(out_3), .out2(out_4), .sel(counter_1_q));  // open: out3, in, en
endmodule
