// Logisim project tests.circ as structural Verilog: 2 circuits, main circuit main
module main (
  input  in_1,
  output out_2
);

  wire and_1_out, and_2_out, and_3_out, and_4_out, and_5_out, and_6_out, and_7_out, d_ff_1_q, d_ff_2_q,
       d_ff_3_q, d_ff_4_q, n2phaseclock_1_out_1, n2phaseclock_1_out_2, not_1_out, or_1_out, or_2_out;

  _2phaseclock u_2phaseclock_1 (.out_1(n2phaseclock_1_out_1), .out_2(n2phaseclock_1_out_2));
  D_Flip_Flop d_ff_1 (.clk(n2phaseclock_1_out_1), .D(or_1_out), .Q(d_ff_1_q));  // open: Qn, preset, en, reset
  or or_1 (or_1_out, and_2_out, and_1_out);
  and and_1 (and_1_out, in_1, not_1_out);
  and and_2 (and_2_out, d_ff_2_q, d_ff_4_q);
  D_Flip_Flop d_ff_2 (.clk(n2phaseclock_1_out_2), .D(d_ff_1_q), .Q(d_ff_2_q));  // open: Qn, preset, en, reset
  and and_3 (and_3_out, d_ff_4_q, d_ff_2_q);
  not not_1 (not_1_out, d_ff_2_q);
  D_Flip_Flop d_ff_3 (.clk(n2phaseclock_1_out_1), .D(or_2_out), .Q(d_ff_3_q));  // open: Qn, preset, en, reset
  or or_2 (or_2_out, and_3_out, and_4_out, and_5_out);
  and and_4 (and_4_out, in_1, d_ff_2_q);
  and and_5 (and_5_out, in_1, d_ff_4_q);
  D_Flip_Flop d_ff_4 (.clk(n2phaseclock_1_out_2), .D(d_ff_3_q), .Q(d_ff_4_q));  // open: Qn, preset, en, reset
  or or_3 (out_2, and_7_out, and_6_out);
  and and_6 (and_6_out, d_ff_4_q, in_1);
  and and_7 (and_7_out, d_ff_2_q, d_ff_4_q);
endmodule

module _2phaseclock (
  output out_1,
  output out_2
);

  wire clock_1_out, d_ff_1_q, d_ff_1_qn, d_ff_2_q, d_ff_2_qn;

  Clock clock_1 (.out(clock_1_out));
  D_Flip_Flop d_ff_1 (.clk(clock_1_out), .D(d_ff_1_qn), .Q(d_ff_1_q), .Qn(d_ff_1_qn));  // open: preset, en, reset
  D_Flip_Flop d_ff_2 (.clk(d_ff_1_qn), .D(d_ff_2_qn), .Q(d_ff_2_q), .Qn(d_ff_2_qn));  // open: preset, en, reset
  and and_1 (out_1, ~d_ff_2_q, d_ff_1_q);  // AND_Gate
  and and_2 (out_2, d_ff_2_q, d_ff_1_q);
endmodule
