// Logisim project conway.circ as structural Verilog: 1 circuit, main circuit main
module main (
);

  wire [7:0] undriven, undriven_2, undriven_3, undriven_4, undriven_5, undriven_6, undriven_7, undriven_8;

  DotMatrix #(.matrixcols(8), .matrixrows(8)) dotmatrix_1 (
    .col0(undriven), .col1(undriven_2), .col2(undriven_3), .col3(undriven_4), .col4(undriven_5),
    .col5(undriven_6), .col6(undriven_7), .col7(undriven_8));
endmodule
