// Logisim project operators.circ as structural Verilog: 6 circuits, main circuit NAND
module main (
  input  in_1,
  input  in_2
);

  wire and_1_out_3, nand_1_out_3, nor_1_out_3, or_1_out_3;

  NAND nand_1 (.in_1(in_1), .in_2(in_2), .out_3(nand_1_out_3));
  NOR nor_1 (.in_1(in_1), .in_2(in_2), .out_3(nor_1_out_3));
  AND and_1 (.in_1(in_1), .in_2(in_2), .out_3(and_1_out_3));
  OR or_1 (.in_1(in_1), .in_2(in_2), .out_3(or_1_out_3));
endmodule

module NAND (
  input  in_1,
  input  in_2,
  output out_3
);

  wire transistor_3_out, transistor_4_out;

  Transistor transistor_1 (.in(1'b1), .out(out_3), .gate(in_1));
  Transistor transistor_2 (.in(1'b1), .out(out_3), .gate(in_2));
  Transistor #(.\type ("n")) transistor_3 (.in(out_3), .out(transistor_3_out), .gate(in_1));
  Transistor #(.\type ("n")) transistor_4 (.in(transistor_3_out), .out(transistor_4_out), .gate(in_2));
  Pull_Resistor pull_resistor_1 (.node(out_3));
  // also tied to GND on the sheet: transistor_4_out
endmodule

module NOR (
  input  in_1,
  input  in_2,
  output out_3
);

  wire transistor_1_out, transistor_2_out;

  Transistor #(.\type ("n")) transistor_1 (.in(out_3), .out(transistor_1_out), .gate(in_2));
  Transistor transistor_2 (.in(1'b1), .out(transistor_2_out), .gate(in_1));
  Transistor transistor_3 (.in(transistor_2_out), .out(out_3), .gate(in_2));
  Transistor #(.\type ("n")) transistor_4 (.in(out_3), .out(transistor_1_out), .gate(in_1));
  Pull_Resistor pull_resistor_1 (.node(out_3));
  // also tied to GND on the sheet: transistor_1_out
endmodule

module NOT (
  input  in_1,
  output out_2
);

  wire transistor_2_out;

  Transistor transistor_1 (.in(1'b1), .out(out_2), .gate(in_1));
  Transistor #(.\type ("n")) transistor_2 (.in(out_2), .out(transistor_2_out), .gate(in_1));
  Pull_Resistor pull_resistor_1 (.node(out_2));
  // also tied to GND on the sheet: transistor_2_out
endmodule

module AND (
  input  in_1,
  input  in_2,
  output out_3
);

  wire transistor_1_out, transistor_3_out, transistor_4_out;

  Transistor transistor_1 (.in(1'b1), .out(transistor_1_out), .gate(in_1));
  Transistor transistor_2 (.in(1'b1), .out(transistor_1_out), .gate(in_2));
  Pull_Resistor pull_resistor_1 (.node(transistor_1_out));
  Transistor #(.\type ("n")) transistor_3 (.in(transistor_1_out), .out(transistor_3_out), .gate(in_1));
  Transistor #(.\type ("n")) transistor_4 (.in(transistor_3_out), .out(transistor_4_out), .gate(in_2));
  Transistor transistor_5 (.in(1'b1), .out(out_3), .gate(transistor_1_out));
  Transistor #(.\type ("n")) transistor_6 (.in(out_3), .out(transistor_4_out), .gate(transistor_1_out));
  Pull_Resistor pull_resistor_2 (.node(out_3));
  // also tied to GND on the sheet: transistor_4_out
endmodule

module OR (
  input  in_1,
  input  in_2,
  output out_3
);

  wire transistor_1_out, transistor_2_out, transistor_3_out;

  Transistor #(.\type ("n")) transistor_1 (.in(transistor_3_out), .out(transistor_1_out), .gate(in_2));
  Transistor transistor_2 (.in(1'b1), .out(transistor_2_out), .gate(in_1));
  Transistor transistor_3 (.in(transistor_2_out), .out(transistor_3_out), .gate(in_2));
  Pull_Resistor pull_resistor_1 (.node(transistor_3_out));
  Transistor #(.\type ("n")) transistor_4 (.in(transistor_3_out), .out(transistor_1_out), .gate(in_1));
  Transistor transistor_5 (.in(1'b1), .out(out_3), .gate(transistor_3_out));
  Transistor #(.\type ("n")) transistor_6 (.in(out_3), .out(transistor_1_out), .gate(transistor_3_out));
  Pull_Resistor pull_resistor_2 (.node(out_3));
  // also tied to GND on the sheet: transistor_1_out
endmodule
